# Fritzing sketch cascade_trigger_02 (saved by Fritzing 0.9.3b)
circuit board: 14.69cm x 8.36cm

parts:
  Teensy = Teensy 3.6 (Basic)
  100µF1 = Electrolytic Capacitor [capacitance=100µF voltage=16V package="100 mil [THT, electrolytic]"]
  100pF1 = Ceramic Capacitor [capacitance=2nF package="100 mil [THT, multilayer]"]
  status_leds_1 = shrouded pin header, 14 pins [form="♂ (shrouded male)"]
  status_leds_2 = shrouded pin header, 14 pins [form="♂ (shrouded male)"]
  T1_1 = SMA Antenna Connector RA 6mm pad spacing
  driv_1 = IC, DIP package, 8 pins [chip_label=EL7104]
  100µF = Electrolytic Capacitor [capacitance=4.7µF voltage=16V package="100 mil [THT, electrolytic]"]
  T1_2 = SMA Antenna Connector RA 6mm pad spacing
  Pdwn_10k = Resistor [tolerance=±5% resistance=10k package=THT]
  termin_1 = IC, DIP package, 8 pins [chip_label=term]
  Pdwn_10k1 = Resistor [tolerance=±5% resistance=10k package=THT]
  100pF2 = Ceramic Capacitor [capacitance=2nF package="100 mil [THT, multilayer]"]
  100µF2 = Electrolytic Capacitor [capacitance=4.7µF voltage=16V package="100 mil [THT, electrolytic]"]
  T1_3 = SMA Antenna Connector RA 6mm pad spacing
  T1_4 = SMA Antenna Connector RA 6mm pad spacing
  driv_2 = IC, DIP package, 8 pins [chip_label=EL7104]
  termin_2 = IC, DIP package, 8 pins [chip_label=term]
  Pdwn_10k2 = Resistor [tolerance=±5% resistance=10k package=THT]
  100pF3 = Ceramic Capacitor [capacitance=2nF package="100 mil [THT, multilayer]"]
  100µF3 = Electrolytic Capacitor [capacitance=4.7µF voltage=16V package="100 mil [THT, electrolytic]"]
  T1_5 = SMA Antenna Connector RA 6mm pad spacing
  T1_6 = SMA Antenna Connector RA 6mm pad spacing
  driv_3 = IC, DIP package, 8 pins [chip_label=EL7104]
  termin_3 = IC, DIP package, 8 pins [chip_label=term]
  Pdwn_10k3 = Resistor [tolerance=±5% resistance=10k package=THT]
  100pF4 = Ceramic Capacitor [capacitance=2nF package="100 mil [THT, multilayer]"]
  100µF4 = Electrolytic Capacitor [capacitance=4.7µF voltage=16V package="100 mil [THT, electrolytic]"]
  T1_7 = SMA Antenna Connector RA 6mm pad spacing
  T1_8 = SMA Antenna Connector RA 6mm pad spacing
  driv_4 = IC, DIP package, 8 pins [chip_label=EL7104]
  termin_4 = IC, DIP package, 8 pins [chip_label=term]
  Pdwn_10k4 = Resistor [tolerance=±5% resistance=10k package=THT]
  100pF5 = Ceramic Capacitor [capacitance=2nF package="100 mil [THT, multilayer]"]
  100µF5 = Electrolytic Capacitor [capacitance=4.7µF voltage=16V package="100 mil [THT, electrolytic]"]
  T1_9 = SMA Antenna Connector RA 6mm pad spacing
  T1_10 = SMA Antenna Connector RA 6mm pad spacing
  driv_5 = IC, DIP package, 8 pins [chip_label=EL7104]
  termin_5 = IC, DIP package, 8 pins [chip_label=term]
  Pdwn_10k5 = Resistor [tolerance=±5% resistance=10k package=THT]
  100pF6 = Ceramic Capacitor [capacitance=2nF package="100 mil [THT, multilayer]"]
  100µF6 = Electrolytic Capacitor [capacitance=4.7µF voltage=16V package="100 mil [THT, electrolytic]"]
  T1_11 = SMA Antenna Connector RA 6mm pad spacing
  T1_12 = SMA Antenna Connector RA 6mm pad spacing
  driv_6 = IC, DIP package, 8 pins [chip_label=EL7104]
  termin_6 = IC, DIP package, 8 pins [chip_label=term]
  Pdwn_10k6 = Resistor [tolerance=±5% resistance=10k package=THT]
  100pF7 = Ceramic Capacitor [capacitance=2nF package="100 mil [THT, multilayer]"]
  100µF7 = Electrolytic Capacitor [capacitance=4.7µF voltage=16V package="100 mil [THT, electrolytic]"]
  T1_13 = SMA Antenna Connector RA 6mm pad spacing
  T1_14 = SMA Antenna Connector RA 6mm pad spacing
  driv_7 = IC, DIP package, 8 pins [chip_label=EL7104]
  termin_7 = IC, DIP package, 8 pins [chip_label=term]
  J1 = Screw terminal - 2 pins [package=THT]
  Pdwn_10k7 = Resistor [tolerance=±5% resistance=10k package=THT]
  100pF8 = Ceramic Capacitor [capacitance=2nF package="100 mil [THT, multilayer]"]
  100µF8 = Electrolytic Capacitor [capacitance=4.7µF voltage=16V package="100 mil [THT, electrolytic]"]
  T1_15 = SMA Antenna Connector RA 6mm pad spacing
  T1_16 = SMA Antenna Connector RA 6mm pad spacing
  driv_8 = IC, DIP package, 8 pins [chip_label=EL7104]
  termin_8 = IC, DIP package, 8 pins [chip_label=term]
  100µF9 = Electrolytic Capacitor [capacitance=100µF voltage=16V package="100 mil [THT, electrolytic]"]
  100pF9 = Ceramic Capacitor [capacitance=22nF package="100 mil [THT, multilayer]"]
  trig_in_1 = SMA Antenna Connector RA 6mm pad spacing
  Pdwn_10k9 = Resistor [tolerance=±5% resistance=10k package=THT]
  trig_in_2 = SMA Antenna Connector RA 6mm pad spacing
  Pdwn_10k10 = Resistor [tolerance=±5% resistance=10k package=THT]
  Pdwn_10k11 = Resistor [tolerance=±5% resistance=10k package=THT]
  trig_in_3 = SMA Antenna Connector RA 6mm pad spacing
  trig_in_4 = SMA Antenna Connector RA 6mm pad spacing
  R_LED = Resistor [tolerance=±5% resistance=56 package=THT]
  P_LED_(56O) = LED - 5mm [color="Red (633nm)" package="5 mm [THT]"]
  R_LED_1 = Resistor [tolerance=±5% resistance=56 package=THT]
  R_LED_2 = Resistor [tolerance=±5% resistance=56 package=THT]
  R_LED_3 = Resistor [tolerance=±5% resistance=56 package=THT]
  R_LED_4 = Resistor [tolerance=±5% resistance=56 package=THT]
  R_LED_5 = Resistor [tolerance=±5% resistance=56 package=THT]
  R_LED_6 = Resistor [tolerance=±5% resistance=56 package=THT]
  R_LED_7 = Resistor [tolerance=±5% resistance=56 package=THT]
  R_LED_8 = Resistor [tolerance=±5% resistance=56 package=THT]
  Pdwn_10k8 = Resistor [tolerance=±5% resistance=10k package=THT]

nets:
  GND: Teensy.GND, Teensy.AGND, 100µF1.-, 100pF1.1, status_leds_1.pin8, status_leds_1.pin9, status_leds_1.pin10, status_leds_1.pin11, status_leds_1.pin12, status_leds_1.pin13, status_leds_1.pin14, status_leds_2.pin8, status_leds_2.pin9, status_leds_2.pin10, status_leds_2.pin11, status_leds_2.pin12, status_leds_2.pin13, status_leds_2.pin14, T1_1.GND, driv_1.pin4, driv_1.pin5, 100µF.-, T1_2.GND, Pdwn_10k.Pin_0, termin_1.pin5, termin_1.pin6, termin_1.pin7, termin_1.pin8, Pdwn_10k6.Pin_0, 100pF7.1, 100µF7.-, T1_13.GND, T1_14.GND, driv_7.pin4, driv_7.pin5, termin_7.pin5, termin_7.pin6, termin_7.pin7, termin_7.pin8, J1.pin1, Pdwn_10k7.Pin_0, 100pF8.1, 100µF8.-, T1_15.GND, T1_16.GND, driv_8.pin4, driv_8.pin5, termin_8.pin5, termin_8.pin6, termin_8.pin7, termin_8.pin8, 100µF9.-, 100pF9.1, trig_in_1.GND, Pdwn_10k9.Pin_0, trig_in_2.GND, Pdwn_10k10.Pin_0, Pdwn_10k11.Pin_0, trig_in_3.GND, trig_in_4.GND, R_LED.Pin_0, Pdwn_10k8.Pin_0
  N1: Teensy.D2, R_LED_7.Pin_0
  N2: Teensy.D5, R_LED_1.Pin_0
  N3: Teensy.D6, R_LED_4.Pin_0
  N4: Teensy.D7, R_LED_6.Pin_0
  N5: Teensy.D8, R_LED_5.Pin_0
  N6: Teensy.D9, Pdwn_10k3.Pin_1, driv_4.pin2
  N7: Teensy.D10, Pdwn_10k2.Pin_1, driv_3.pin2
  N8: Teensy.D11, Pdwn_10k1.Pin_1, driv_2.pin2
  N9: Teensy.D12, driv_1.pin2, Pdwn_10k.Pin_1
  N10: Teensy.D13, Pdwn_10k7.Pin_1, driv_8.pin2
  N11: Teensy.A0/D14, R_LED_3.Pin_1
  N12: Teensy.A1/D15, Pdwn_10k6.Pin_1, driv_7.pin2
  N13: Teensy.A2/D16, trig_in_1.SIGNAL, Pdwn_10k8.Pin_1
  N14: Teensy.A3/D17, Pdwn_10k9.Pin_1, trig_in_2.SIGNAL
  N15: Teensy.A6/D20, R_LED_8.Pin_0
  N16: Teensy.A7/D21, R_LED_2.Pin_1
  N17: Teensy.A8/D22, Pdwn_10k5.Pin_1, driv_6.pin2
  N18: Teensy.A9/D23, Pdwn_10k4.Pin_1, driv_5.pin2
  5V: Teensy.Vin, 100µF1.+, driv_1.pin1, driv_1.pin8, 100µF.+, 100µF2.+, driv_2.pin1, driv_2.pin8, 100µF3.+, driv_3.pin1, driv_3.pin8, 100µF4.+, driv_4.pin1, driv_4.pin8, 100µF5.+, driv_5.pin1, driv_5.pin8, 100µF6.+, driv_6.pin1, driv_6.pin8, 100µF7.+, driv_7.pin1, driv_7.pin8, J1.pin2, 100µF8.+, driv_8.pin1, driv_8.pin8, 100µF9.+, 100pF9.0, P_LED_(56O).anode
  N19: 100pF1.0, driv_1.pin6
  N20: status_leds_1.pin1, R_LED_1.Pin_1
  N21: status_leds_1.pin2, R_LED_2.Pin_0
  N22: status_leds_1.pin3, R_LED_4.Pin_1
  N23: status_leds_1.pin4, R_LED_5.Pin_1
  N24: status_leds_1.pin5, R_LED_6.Pin_1
  N25: status_leds_1.pin6, R_LED_3.Pin_0
  N26: status_leds_1.pin7, R_LED_7.Pin_1
  N27: status_leds_2.pin1, R_LED_8.Pin_1
  N28: T1_1.SIGNAL, driv_1.pin7, T1_2.SIGNAL, termin_1.pin1, termin_1.pin2, termin_1.pin3, termin_1.pin4
  GND_2: Pdwn_10k1.Pin_0, 100pF2.1, 100µF2.-, T1_3.GND, T1_4.GND, driv_2.pin4, driv_2.pin5, termin_2.pin5, termin_2.pin6, termin_2.pin7, termin_2.pin8
  N29: 100pF2.0, driv_2.pin6
  N30: T1_3.SIGNAL, T1_4.SIGNAL, driv_2.pin7, termin_2.pin1, termin_2.pin2, termin_2.pin3, termin_2.pin4
  GND_3: Pdwn_10k2.Pin_0, 100pF3.1, 100µF3.-, T1_5.GND, T1_6.GND, driv_3.pin4, driv_3.pin5, termin_3.pin5, termin_3.pin6, termin_3.pin7, termin_3.pin8
  N31: 100pF3.0, driv_3.pin6
  N32: T1_5.SIGNAL, T1_6.SIGNAL, driv_3.pin7, termin_3.pin1, termin_3.pin2, termin_3.pin3, termin_3.pin4
  GND_4: Pdwn_10k3.Pin_0, 100pF4.1, 100µF4.-, T1_7.GND, T1_8.GND, driv_4.pin4, driv_4.pin5, termin_4.pin5, termin_4.pin6, termin_4.pin7, termin_4.pin8
  N33: 100pF4.0, driv_4.pin6
  N34: T1_7.SIGNAL, T1_8.SIGNAL, driv_4.pin7, termin_4.pin1, termin_4.pin2, termin_4.pin3, termin_4.pin4
  GND_5: Pdwn_10k4.Pin_0, 100pF5.1, 100µF5.-, T1_9.GND, T1_10.GND, driv_5.pin4, driv_5.pin5, termin_5.pin5, termin_5.pin6, termin_5.pin7, termin_5.pin8
  N35: 100pF5.0, driv_5.pin6
  N36: T1_9.SIGNAL, T1_10.SIGNAL, driv_5.pin7, termin_5.pin1, termin_5.pin2, termin_5.pin3, termin_5.pin4
  GND_6: Pdwn_10k5.Pin_0, 100pF6.1, 100µF6.-, T1_11.GND, T1_12.GND, driv_6.pin4, driv_6.pin5, termin_6.pin5, termin_6.pin6, termin_6.pin7, termin_6.pin8
  N37: 100pF6.0, driv_6.pin6
  N38: T1_11.SIGNAL, T1_12.SIGNAL, driv_6.pin7, termin_6.pin1, termin_6.pin2, termin_6.pin3, termin_6.pin4
  N39: 100pF7.0, driv_7.pin6
  N40: T1_13.SIGNAL, T1_14.SIGNAL, driv_7.pin7, termin_7.pin1, termin_7.pin2, termin_7.pin3, termin_7.pin4
  N41: 100pF8.0, driv_8.pin6
  N42: T1_15.SIGNAL, T1_16.SIGNAL, driv_8.pin7, termin_8.pin1, termin_8.pin2, termin_8.pin3, termin_8.pin4
  N43: Pdwn_10k10.Pin_1, trig_in_4.SIGNAL
  N44: Pdwn_10k11.Pin_1, trig_in_3.SIGNAL
  N45: R_LED.Pin_1, P_LED_(56O).cathode

notes:
  cascade trigger v01
  JR 2019 UZH

custom parts:
  Teensy 3.6 (Basic): The Teensy is a complete USB-based microcontoller development system, in a very small footprint, capable of implementing many types of projects. All programming is done via the USB port. No special programmer is needed, only a standard micro-USB cable and a PC or Macintosh with a USB port.
  SMA Antenna Connector RA 6mm pad spacing: SMA RA Antenna Connector with 6mm pcb pad spacing.
